# Fritzing sketch Schéma Fritzing Projet - Groupe 5 (saved by Fritzing 0.9.3b)
breadboards: 1

parts:
  Composant1 = Arduino Uno (Rev3)
  R1 = Resistor [tolerance=±5% resistance=10k package=THT]
  L1 = Inductor [inductance=10mH package="400 mil [THT]"]
  C1 = Ceramic Capacitor [capacitance=10nF package="100 mil [THT, multilayer]"]
  D1 = Rectifier Diode [part_number=1N4001 package="300 mil [THT]"]
  C2 = Ceramic Capacitor [capacitance=0.1nF package="100 mil [THT, multilayer]"]
  R2 = Resistor [tolerance=±5% resistance=1M package=THT]
  R3 = Resistor [tolerance=±5% resistance=220 package=THT]
  R4 = Resistor [tolerance=±5% resistance=220 package=THT]
  LED1 = LED - 3mm [color="Red (633nm)" package="3 mm [THT]"]
  LED2 = LED - 3mm [color="Orange (605nm)" package="3 mm [THT]"]
  R5 = Resistor [tolerance=±5% resistance=220 package=THT]
  R6 = Resistor [tolerance=±5% resistance=220 package=THT]
  LED3 = LED - 3mm [color="Green (555nm)" package="3 mm [THT]"]

nets:
  N1: Composant1.D9_PWM, R1.Pin_1
  N2: Composant1.D2, R4.Pin_0
  N3: Composant1.D4, R5.Pin_0
  N4: Composant1.D7, R6.Pin_0
  N5: Composant1.GND, C2.0, R2.Pin_0, R3.Pin_1, LED1.anode, LED2.anode, LED3.anode
  N6: R1.Pin_0, L1.pin_1, R3.Pin_0
  N7: L1.pin_0, C1.1, D1.anode
  N8: D1.cathode, C2.1, R2.Pin_1
  N9: R4.Pin_1, LED1.cathode
  N10: LED2.cathode, R5.Pin_1
  N11: R6.Pin_1, LED3.cathode
